# Fritzing sketch LaserSketch (saved by Fritzing 0.9.2b)
breadboards: 1

parts:
  Q1 = NPN-Transistor [package="TO92 [THT]"]
  Q2 = NPN-Transistor [package="TO92 [THT]"]
  Q3 = NPN-Transistor [package="TO92 [THT]"]
  R1 = Resistor [tolerance=±5% resistance=220 package=THT]
  R2 = Resistor [tolerance=±5% resistance=220 package=THT]
  R3 = Resistor [tolerance=±5% resistance=220 package=THT]
  D1 = Rectifier Diode [part_number=1N4001 package="300 mil [THT]"]
  D2 = Rectifier Diode [part_number=1N4001 package="300 mil [THT]"]
  D3 = Rectifier Diode [part_number=1N4001 package="300 mil [THT]"]
  Lilypad_Vibe1 = Lilypad Vibe Motor
  Lilypad_Vibe2 = Lilypad Vibe Motor
  Lilypad_Vibe3 = Lilypad Vibe Motor
  Part1 = Arduino Uno (Rev3) - ICSP
  LASER = LED - 5mm [color="Red (660nm)" package="5 mm [THT]"]

nets:
  N1: Q1.E, Q2.E, Q3.E, Part1.GND, LASER.cathode
  N2: Q1.B, R1.Pin_0
  N3: Q1.C, D3.anode, Lilypad_Vibe1.GND
  N4: Q2.B, R2.Pin_0
  N5: Q2.C, D2.anode, Lilypad_Vibe2.GND
  N6: Q3.B, R3.Pin_0
  N7: Q3.C, D1.anode, Lilypad_Vibe3.GND
  N8: R1.Pin_1, Part1.D5_PWM
  N9: R2.Pin_1, Part1.D4
  N10: R3.Pin_1, Part1.D3_PWM
  N11: D1.cathode, D2.cathode, D3.cathode, Lilypad_Vibe1.Supply, Lilypad_Vibe2.Supply, Lilypad_Vibe3.Supply, Part1.5V
  N12: Part1.D13/SCK, LASER.anode
